# Fritzing sketch Amiacs Arcade (saved by Fritzing 1.0.2b)

parts:
  Part1 = 24-Channel 12-bit PWM LED Driver - SPI [part_number=1429]
  Part2 = Arduino Nano (Rev3.0) (ICSP)
  D1 = Rectifier Diode [part_number=1N4001 package="300 mil [THT]"]
  J6 = single row smd female pin header, 2 pins [form="♀ (female)"]
  JST_SM-2 = single row smd male pin header, 2 pins [form="♂ (male)"]
  JST_SM-1 = double row smd male pin header, 2 pins [form="♂ (male)"]
  JST_SM-3 = single row smd female pin header, 2 pins [form="♀ (female)"]
  J7 = double row smd male pin header, 2 pins [form="♂ (male)"]
  J8 = single row smd female pin header, 2 pins [form="♀ (female)"]
  B-1 = Pushbutton [package=THT]
  K12-1 = female pin header, 3 pins [form="♀ (female)"]
  LED2 = LED - 5mm [color="Blue (525nm)" current=0.030 package="5 mm [THT]"]
  Player_1 = USB connector [package=THT]  # not connected
  K11-1 = female pin header, 3 pins [form="♀ (female)"]
  ST-1 = female pin header, 3 pins [form="♀ (female)"]
  SE-1 = female pin header, 3 pins [form="♀ (female)"]
  R1-1 = female pin header, 3 pins [form="♀ (female)"]
  L1-1 = female pin header, 3 pins [form="♀ (female)"]
  R2-1 = female pin header, 3 pins [form="♀ (female)"]
  L2-1 = female pin header, 3 pins [form="♀ (female)"]
  K4-1 = female pin header, 3 pins [form="♀ (female)"]
  K3-1 = female pin header, 3 pins [form="♀ (female)"]
  K2-1 = female pin header, 3 pins [form="♀ (female)"]
  K1-1 = female pin header, 3 pins [form="♀ (female)"]
  A-1 = Pushbutton [package=THT]
  LED3 = LED - 5mm [color="Blue (525nm)" current=0.030 package="5 mm [THT]"]
  L1-1_2 = Pushbutton [package=THT]
  LED4 = LED - 5mm [color="Blue (525nm)" current=0.030 package="5 mm [THT]"]
  R1-1_2 = Pushbutton [package=THT]
  LED5 = LED - 5mm [color="Blue (525nm)" current=0.030 package="5 mm [THT]"]
  Y-1 = Pushbutton [package=THT]
  L2-1_2 = Pushbutton [package=THT]
  X-1 = Pushbutton [package=THT]
  R2-1_2 = Pushbutton [package=THT]
  LED6 = LED - 5mm [color="Blue (525nm)" current=0.030 package="5 mm [THT]"]
  LED7 = LED - 5mm [color="Blue (525nm)" current=0.030 package="5 mm [THT]"]
  LED8 = LED - 5mm [color="Blue (525nm)" current=0.030 package="5 mm [THT]"]
  LED9 = LED - 5mm [color="Blue (525nm)" current=0.030 package="5 mm [THT]"]
  EXIT-1 = Pushbutton [package=THT]
  LED10 = LED - 5mm [color="Yellow (595nm)" current=0.030 package="5 mm [THT]"]
  START-1 = Pushbutton [package=THT]
  SELECT-1 = Pushbutton [package=THT]
  LED11 = LED - 5mm [color="Blue (525nm)" current=0.030 package="5 mm [THT]"]
  LED12 = LED - 5mm [color="Blue (525nm)" current=0.030 package="5 mm [THT]"]
  HOTKEY-1 = Pushbutton [package=THT]
  LED13 = LED - 5mm [color="Yellow (595nm)" current=0.030 package="5 mm [THT]"]
  JOY1 = Adafruit Arcade Joystick  # not connected
  D3 = Rectifier Diode [part_number=1N4001 package="300 mil [THT]"]
  SELECT-2 = Pushbutton [package=THT]
  START-2 = Pushbutton [package=THT]
  EXIT-2 = Pushbutton [package=THT]
  R2-2 = Pushbutton [package=THT]
  X-2 = Pushbutton [package=THT]
  L2-2 = Pushbutton [package=THT]
  Y-2 = Pushbutton [package=THT]
  R1-2 = Pushbutton [package=THT]
  L1-2 = Pushbutton [package=THT]
  A-2 = Pushbutton [package=THT]
  B-2 = Pushbutton [package=THT]
  K1-2 = female pin header, 3 pins [form="♀ (female)"]
  K2-2 = female pin header, 3 pins [form="♀ (female)"]
  K3-2 = female pin header, 3 pins [form="♀ (female)"]
  K4-2 = female pin header, 3 pins [form="♀ (female)"]
  L2-2_2 = female pin header, 3 pins [form="♀ (female)"]
  R2-2_2 = female pin header, 3 pins [form="♀ (female)"]
  L1-2_2 = female pin header, 3 pins [form="♀ (female)"]
  R1-2_2 = female pin header, 3 pins [form="♀ (female)"]
  SE-2 = female pin header, 3 pins [form="♀ (female)"]
  ST-2 = female pin header, 3 pins [form="♀ (female)"]
  K11-2 = female pin header, 3 pins [form="♀ (female)"]
  K12-2 = female pin header, 3 pins [form="♀ (female)"]
  LED14 = LED - 5mm [color="Red (660nm)" current=0.030 package="5 mm [THT]"]
  LED15 = LED - 5mm [color="Red (660nm)" current=0.030 package="5 mm [THT]"]
  LED16 = LED - 5mm [color="Yellow (595nm)" current=0.030 package="5 mm [THT]"]
  LED17 = LED - 5mm [color="Red (660nm)" current=0.030 package="5 mm [THT]"]
  LED18 = LED - 5mm [color="Red (660nm)" current=0.030 package="5 mm [THT]"]
  LED19 = LED - 5mm [color="Red (660nm)" current=0.030 package="5 mm [THT]"]
  LED20 = LED - 5mm [color="Red (660nm)" current=0.030 package="5 mm [THT]"]
  LED21 = LED - 5mm [color="Red (660nm)" current=0.030 package="5 mm [THT]"]
  LED22 = LED - 5mm [color="Red (660nm)" current=0.030 package="5 mm [THT]"]
  LED23 = LED - 5mm [color="Red (660nm)" current=0.030 package="5 mm [THT]"]
  LED24 = LED - 5mm [color="Red (660nm)" current=0.030 package="5 mm [THT]"]
  Player_2 = USB connector [package=THT]  # not connected
  JOY2 = Adafruit Arcade Joystick  # not connected
  HOTKEY-2 = Pushbutton [package=THT]
  LED25 = LED - 5mm [color="Yellow (595nm)" current=0.030 package="5 mm [THT]"]
  J13 = shrouded pin header, 28 pins [form="♂ (shrouded male)"]
  OPTI-WIZ = USB connector [package=THT]  # not connected
  TRACKBALL = female pin header, 6 pins [form="♀ (female)"]
  J14 = single row smd female pin header, 4 pins [form="♀ (female)"]
  JST_SM-6 = double row smd male pin header, 4 pins [form="♂ (male)"]
  Raspberry_Pi_1 = Raspberry Pi 3 [part_number=RPI-3-V1.2]
  EXTERNAL = USB connector [package=THT]  # not connected
  LiFePO4wered/Pi+_18650_3_2V = Lithium Ion Cylindrical Battery 3.7v 2200mAh
  J12 = single row smd male pin header, 2 pins [form="♂ (male)"]
  JST_SM-5 = double row smd female pin header, 2 pins [form="♀ (female)"]
  JST_SM-4 = double row smd female pin header, 4 pins [form="♀ (female)"]
  J10 = single row smd male pin header, 4 pins [form="♂ (male)"]
  D5 = Rectifier Diode [part_number=1N4001 package="300 mil [THT]"]
  J15 = single row smd male pin header, 4 pins [form="♂ (male)"]
  JST_SM-7 = double row smd female pin header, 4 pins [form="♀ (female)"]
  JACK1 = 2.1mm DC Barrel Jack
  J16 = single row smd male pin header, 2 pins [form="♂ (male)"]
  JST_SM-8 = double row smd female pin header, 2 pins [form="♀ (female)"]
  VIN = double row smd female pin header, 2 pins [form="♀ (female)"]
  Mean_Well_RD-65A_Power_Supply = screw terminal, 7 pins
  SP1 = SPEAKER [package=pcb_mount_speaker]
  SP2 = SPEAKER [package=pcb_mount_speaker]
  RGB_Strip_LED1 = RGB Strip LED
  RGB_Strip_LED2 = RGB Strip LED
  RGB_Strip_LED3 = RGB Strip LED
  RGB_Strip_LED4 = RGB Strip LED
  LED27 = LED - 5mm [color="White (4500K)" current=0.030 package="5 mm [THT]"]
  J22 = Camdenboss CTB0158-2 [part_number=CTB0158-2 package=THT]
  J23 = Camdenboss CTB0158-4 [part_number=CTB0158-4 package=THT]
  J24 = single row smd male pin header, 4 pins [form="♂ (male)"]
  J25 = single row smd male pin header, 4 pins [form="♂ (male)"]
  J26 = single row smd male pin header, 4 pins [form="♂ (male)"]
  J27 = single row smd male pin header, 4 pins [form="♂ (male)"]
  J28 = Camdenboss CTB0158-2 [part_number=CTB0158-2 package=THT]
  J29 = Camdenboss CTB0158-4 [part_number=CTB0158-4 package=THT]
  J20 = single row smd female pin header, 4 pins [form="♀ (female)"]
  JST_SM-9 = double row smd male pin header, 4 pins [form="♂ (male)"]  # not connected
  J21 = single row smd female pin header, 4 pins [form="♀ (female)"]
  JST_SM-10 = double row smd male pin header, 4 pins [form="♂ (male)"]  # not connected
  JST_SM-11 = female pin header, 5 pins [form="♀ (female)"]
  J31 = male pin header, 5 pins [form="♂ (male)"]
  J32 = Camdenboss CTB0158-2 [part_number=CTB0158-2 package=THT]  # not connected
  J33 = Camdenboss CTB0158-2 [part_number=CTB0158-2 package=THT]
  J34 = female pin header, 4 pins [form="♀ (female)"]
  J35 = single row smd female pin header, 4 pins [form="♀ (female)"]
  JST_SM-12 = double row smd male pin header, 4 pins [form="♂ (male)"]
  JACK2 = 2.1mm DC Barrel Jack
  J36 = single row smd male pin header, 4 pins [form="♂ (male)"]
  JST_SM-13 = double row smd female pin header, 4 pins [form="♀ (female)"]
  +5V_J1 = male pin header, 6 pins [form="♂ (male)"]  # not connected
  J37 = female pin header, 6 pins [form="♀ (female)"]
  GND_J2 = male pin header, 6 pins [form="♂ (male)"]  # not connected
  J38 = female pin header, 6 pins [form="♀ (female)"]
  J3 = male pin header, 1 pin [form="♂ (male)"]
  J39 = female pin header, 1 pin [form="♀ (female)"]
  R1 = Rotary Potentiometer (Small) [maximum_resistance=1kΩ knob_status=50% power=0.5W package=THT]
  JST_SM-14 = female pin header, 3 pins [form="♀ (female)"]
  J41 = male pin header, 3 pins [form="♂ (male)"]
  J43 = female pin header, 1 pin [form="♀ (female)"]
  J42 = single row smd male pin header, 2 pins [form="♂ (male)"]
  JST_SM-15 = double row smd female pin header, 2 pins [form="♀ (female)"]
  Part3 = Adafruit MAX9744 20W Amplifier [part_number="Adafruit #1752"]
  R2 = Rotary Potentiometer (Small) [maximum_resistance=1kΩ knob_status=50% power=0.5W package=THT]
  LED26 = RGB LED (com. cathode, rgb) [color="Red (633nm)" current=0.030A package="5 mm [THT]"]

nets:
  N1: Part1.LAT, JST_SM-4.pin1
  N2: Part1.OE, JST_SM-4.pin2
  N3: Part1.CLK, JST_SM-4.pin3
  N4: Part1.DIN, JST_SM-4.pin4
  N5: Part1.GND, J7.pin2, JST_SM-5.pin1
  N6: Part1.+24V, J7.pin1
  N7: Part1.PWM0, LED2.anode
  N8: Part1.PWM1, LED3.anode
  N9: Part1.PWM2, LED6.anode
  N10: Part1.PWM3, LED9.anode
  N11: Part1.PWM4, LED8.anode
  N12: Part1.PWM5, LED7.anode
  N13: Part1.PWM6, LED4.anode
  N14: Part1.PWM7, LED5.anode
  N15: Part1.PWM8, LED11.anode
  N16: Part1.PWM9, LED12.anode
  N17: Part1.PWM10, LED10.anode
  N18: Part1.PWM11, LED13.anode
  N19: Part1.PWM12, LED24.anode
  N20: Part1.PWM13, LED23.anode
  N21: Part1.PWM14, LED20.anode
  N22: Part1.PWM15, LED17.anode
  N23: Part1.PWM16, LED18.anode
  N24: Part1.PWM17, LED19.anode
  N25: Part1.PWM18, LED22.anode
  N26: Part1.PWM19, LED21.anode
  N27: Part1.PWM20, LED15.anode
  N28: Part1.PWM21, LED14.anode
  N29: Part1.PWM22, LED16.anode
  N30: Part1.PWM23, LED25.anode
  N31: Part2.D3, J14.pin2
  N32: Part2.D4, Part2.D5, J14.pin3
  N33: Part2.D6, J14.pin4
  N34: Part2.D7, Part2.D8, J10.pin3
  N35: Part2.D9, JST_SM-11.pin1
  N36: Part2.D10, J10.pin4
  N37: Part2.D11/MOSI, JST_SM-11.pin3
  N38: Part2.D12/MISO, J10.pin1
  N39: Part2.GND, J38.pin1
  N40: Part2.5V, J37.pin1
  N41: Part2.A7, JST_SM-14.pin1
  N42: Part2.A5, J15.pin3
  N43: Part2.A4, J15.pin4
  N44: Part2.AREF, Part2.3V3, Part2.D13/SCK, J10.pin2, JST_SM-11.pin2
  N45: D1.cathode, JST_SM-3.pin2, D3.cathode
  N46: D1.anode, J6.pin2, JST_SM-1.pin1, EXIT-2.leg0, K11-2.pin1, LED16.cathode
  N47: J6.pin1, JST_SM-2.pin2, JST_SM-1.pin2, JST_SM-3.pin1, K11-2.pin3
  N48: JST_SM-2.pin1, D3.anode
  N49: J8.pin1, K11-1.pin3
  N50: J8.pin2, K11-1.pin1, EXIT-1.leg0, LED10.cathode
  N51: B-1.leg0, LED2.cathode, K1-1.pin1
  N52: B-1.leg1, K1-1.pin2
  N53: K12-1.pin1, HOTKEY-1.leg0, LED13.cathode
  N54: K12-1.pin2, HOTKEY-1.leg1
  N55: K11-1.pin2, EXIT-1.leg1
  N56: ST-1.pin1, START-1.leg0, LED12.cathode
  N57: ST-1.pin2, START-1.leg1
  N58: SE-1.pin1, SELECT-1.leg0, LED11.cathode
  N59: SE-1.pin2, SELECT-1.leg1
  N60: R1-1.pin1, R1-1_2.leg0, LED5.cathode
  N61: R1-1.pin2, R1-1_2.leg1
  N62: L1-1.pin1, L1-1_2.leg0, LED4.cathode
  N63: L1-1.pin2, L1-1.pin3, L1-1_2.leg1
  N64: R2-1.pin1, R2-1_2.leg0, LED7.cathode
  N65: R2-1.pin2, R2-1_2.leg1
  N66: L2-1.pin1, L2-1_2.leg0, LED8.cathode
  N67: L2-1.pin2, L2-1_2.leg1
  N68: K4-1.pin1, X-1.leg0, LED9.cathode
  N69: K4-1.pin2, X-1.leg1
  N70: K3-1.pin1, Y-1.leg0, LED6.cathode
  N71: K3-1.pin2, Y-1.leg1
  N72: K2-1.pin1, A-1.leg0, LED3.cathode
  N73: K2-1.pin2, A-1.leg1
  N74: SELECT-2.leg0, SE-2.pin1, LED15.cathode
  N75: SELECT-2.leg1, SE-2.pin2
  N76: START-2.leg0, ST-2.pin1, LED14.cathode
  N77: START-2.leg1, ST-2.pin2
  N78: EXIT-2.leg1, K11-2.pin2
  N79: R2-2.leg0, R2-2_2.pin1, LED19.cathode
  N80: R2-2.leg1, R2-2_2.pin2
  N81: X-2.leg0, K4-2.pin1, LED17.cathode
  N82: X-2.leg1, K4-2.pin2
  N83: L2-2.leg0, L2-2_2.pin1, LED18.cathode
  N84: L2-2.leg1, L2-2_2.pin2
  N85: Y-2.leg0, K3-2.pin1, LED20.cathode
  N86: Y-2.leg1, K3-2.pin2
  N87: R1-2.leg0, R1-2_2.pin1, LED21.cathode
  N88: R1-2.leg1, R1-2_2.pin2
  N89: L1-2.leg0, L1-2_2.pin1, LED22.cathode
  N90: L1-2.leg1, L1-2_2.pin2
  N91: A-2.leg0, K2-2.pin1, LED23.cathode
  N92: A-2.leg1, K2-2.pin2
  N93: B-2.leg0, K1-2.pin1, LED24.cathode
  N94: B-2.leg1, K1-2.pin2
  N95: K12-2.pin1, HOTKEY-2.leg0, LED25.cathode
  N96: K12-2.pin2, HOTKEY-2.leg1
  N97: J13.pin3, J13.pin4, TRACKBALL.pin2
  N98: J13.pin12, J13.pin13, TRACKBALL.pin3
  N99: J13.pin14, TRACKBALL.pin6
  N100: J13.pin15, TRACKBALL.pin5
  N101: J13.pin16, J13.pin17, TRACKBALL.pin4
  N102: J13.pin25, J13.pin26, TRACKBALL.pin1
  N103: J14.pin1, J37.pin2
  N104: JST_SM-6.pin1, LED26.blue_anode
  N105: JST_SM-6.pin2, LED26.green_anode
  N106: JST_SM-6.pin3, LED26.red_anode
  N107: JST_SM-6.pin4, LED26.common_cathode
  N108: Raspberry_Pi_1.GPIO2, JST_SM-7.pin1
  N109: Raspberry_Pi_1.GPIO3, JST_SM-7.pin2
  N110: LiFePO4wered/Pi+_18650_3_2V.positive, D5.anode
  N111: LiFePO4wered/Pi+_18650_3_2V.negative, JST_SM-7.pin4
  N112: J12.pin2, J38.pin2
  N113: D5.cathode, JST_SM-7.pin3
  N114: J15.pin1, J38.pin3
  N115: J15.pin2, J37.pin3
  N116: JACK1.center, J16.pin2
  N117: JACK1.sleeve, J16.pin1, JST_SM-15.pin2
  N118: JST_SM-8.pin1, VIN.pin1
  N119: JST_SM-8.pin2, VIN.pin2
  N120: Mean_Well_RD-65A_Power_Supply.pin4, J22.pin2, J28.pin2, J33.pin1
  N121: Mean_Well_RD-65A_Power_Supply.pin5, J22.pin1, J28.pin1, J33.pin2
  N122: SP1.+, Part3.LEFT+
  N123: SP1.-, Part3.LEFT-
  N124: SP2.+, Part3.RIGHT+
  N125: SP2.-, Part3.RIGHT-
  N126: RGB_Strip_LED1.Common_Connect#8, JST_SM-12.pin4
  N127: RGB_Strip_LED1.Green_Connect#9, JST_SM-12.pin1
  N128: RGB_Strip_LED1.Red_Connect#10, JST_SM-12.pin2
  N129: RGB_Strip_LED1.Blue_Connect#11, JST_SM-12.pin3
  N130: RGB_Strip_LED1.Common_Connect#12, RGB_Strip_LED2.Common_Connect#8
  N131: RGB_Strip_LED1.Green_Connect#13, RGB_Strip_LED2.Green_Connect#9
  N132: RGB_Strip_LED1.Red_Connect#14, RGB_Strip_LED2.Red_Connect#10
  N133: RGB_Strip_LED1.Blue_Connect#15, RGB_Strip_LED2.Blue_Connect#11
  N134: RGB_Strip_LED2.Common_Connect#12, J20.pin1
  N135: RGB_Strip_LED2.Green_Connect#13, J20.pin4
  N136: RGB_Strip_LED2.Red_Connect#14, J20.pin3
  N137: RGB_Strip_LED2.Blue_Connect#15, J20.pin2
  N138: RGB_Strip_LED3.Common_Connect#8, RGB_Strip_LED4.Common_Connect#12
  N139: RGB_Strip_LED3.Green_Connect#9, RGB_Strip_LED4.Green_Connect#13
  N140: RGB_Strip_LED3.Red_Connect#10, RGB_Strip_LED4.Red_Connect#14
  N141: RGB_Strip_LED3.Blue_Connect#11, RGB_Strip_LED4.Blue_Connect#15
  N142: RGB_Strip_LED3.Common_Connect#12, J36.pin1
  N143: RGB_Strip_LED3.Green_Connect#13, J36.pin4
  N144: RGB_Strip_LED3.Red_Connect#14, J36.pin3
  N145: RGB_Strip_LED3.Blue_Connect#15, J36.pin2
  N146: RGB_Strip_LED4.Common_Connect#8, J21.pin1
  N147: RGB_Strip_LED4.Green_Connect#9, J21.pin4
  N148: RGB_Strip_LED4.Red_Connect#10, J21.pin3
  N149: RGB_Strip_LED4.Blue_Connect#11, J21.pin2
  N150: LED27.cathode, JACK2.sleeve
  N151: LED27.anode, JACK2.center
  N152: J23.pin1, J35.pin2
  N153: J23.pin2, J35.pin3
  N154: J23.pin3, J35.pin4
  N155: J23.pin4, J35.pin1
  N156: J24.pin1, J26.pin1
  N157: J24.pin2, J26.pin2
  N158: J24.pin3, J26.pin3
  N159: J24.pin4, J26.pin4
  N160: J25.pin1, J31.pin5
  N161: J25.pin2, J31.pin4
  N162: J25.pin3, J31.pin3
  N163: J25.pin4, J31.pin2
  N164: J27.pin1, J34.pin4
  N165: J29.pin1, JST_SM-13.pin3
  N166: J29.pin2, JST_SM-13.pin2
  N167: J29.pin3, JST_SM-13.pin1
  N168: J29.pin4, JST_SM-13.pin4
  N169: JST_SM-11.pin4, J37.pin4
  N170: JST_SM-11.pin5, J38.pin4
  N171: J31.pin1, J39.pin1
  N172: J34.pin1, J3.pin1
  N173: J37.pin5, JST_SM-14.pin2
  N174: J38.pin5, JST_SM-14.pin3
  N175: R1.leg1, J41.pin2
  N176: R1.wiper, J41.pin1
  N177: R1.leg2, J41.pin3
  N178: J43.pin1, J42.pin1
  N179: Part3.GND, R2.leg1
  N180: Part3.3.3V, R2.leg2
  N181: Part3.AVOL, R2.wiper

notes:
  The V+ (black) and GND (red) wire colors coming from the controllers are opposite. This connection will look wrong.
  These diodes are used to keep the voltage from going from one controller to the other.
  Most components are representations. The properties do not reflect the actual part.
  The pushbuttons and LEDs represent the arcade buttons.
  The TLC5947 is upside down in the physical panel. So the pins are mirrored from shown.
  The Raspberry Pi is upside down in the physical panel. So the connections are mirrored from shown.
  Connected to VOUT on LiFePO4wered.
  Without this diode, removing power from LiFePO4wered rebooted the Pi without running the shutdown script.
  This power source might not be the best solution. Could try getting power from the Pi's GPIO pins.
  This layout of components represents what is seen when the control panel is bottom up. As in how it would be oriented to access the components.
  Left and right ARE NOT reversed in this view.
  I2C SDA
  I2C SCL
  SPI CLK
  SPI OE
  SPI LAT
  SPI DIN
  Connected to VIN on
  LiFePO4wered.
  Controls Console
  Monitor Cabinet
  AC L
  AC N
  AC GND
  COM
  +V2 (12V)
  +V1 (5V)
  This layout of components represents what is seen from the rear of the cabinet.
  Left and right ARE reversed in this view.
  Marquee Lights
  Represents a white LED strip.
  +12V
  GND
  VCC
  DIN
  CIN
  DO
  CO
  +
  G
  R
  B
  LED Strip Driver Module P9813
  VOUT
  VIN
  MOSFET Trigger Switch Module
  TRIG/PWM
  SPI DOUT
  RIGHT
  LEFT
  Player 1
  Left
  Player 2
  Right
  Ambient Lights
  Left (Player 1)
  Ambient Lights
  Right (Player 2)
  Custom jumpers with male pins wired together
  WARNING!
  This connector is not keyed and can be inserted incorrectly.
  Female HDMI
  Rear Panel Mount Connectors -->
  Wires are 24AWG stranded silicone except for the LiFePOwered VIN power wires.
  Wires are 24AWG stranded silicone. Except for speaker and power supply wires.
  LiFePOwered VIN wires are 22AWG solid for allow higher current.
  22AWG allows 7A instead of 3.5A for 24AWG.
  65mm
  50mm
  55mm
  530mm
  840mm
  510mm
  430mm
  380mm
  330mm
  Red LED Wires for Player 1
  Wire length is 200mm, except for SELECT-1, EXIT-1 and R2-1 which are 225mm.
  Except for SELECT-1, EXIT-1 and R2-1 these are the wires that come with the encoder. The wire is disconnected from the encoder connector and moved to the TLC5947 connector.
  Red wire from K11-1 is used to create a common ground between the encoder and the Arduino Nano.
  Red wire from K11-2 is used to create a common ground between the encoder and the Arduino Nano.
  Red LED Wires for Player 2
  Wire length is 940mm
  Red LED Wires for Player 2
  Wire length: 940mm
  Sleeve length: 710mm
  Because the wires are in a sleeve, the ends are color coded.
  White Red HOTKEY-2
  White Green EXIT-2
  White Blue START-2
  Black Red SELECT-2
  Black Green R1-2
  Black Blue L1-2
  Yellow Red R2-2
  Yellow Green L2-2
  Yellow Blue X-2
  Red Red Y-2
  Red Green A-2
  Red Blue B-2
  230mm
  615mm
  60mm
  170mm
  22AWG Solid
  300mm
  I2C
  Note the location of the black and yellow wires on the encoder connections. They may differ from the default assembly.
  535mm
  150mm
  750mm
  700mm

custom parts:
  24-Channel 12-bit PWM LED Driver - SPI: This breakout board for the TLC5947 PWM driver chip can control 24 separate channels of 12-bit PWM output. Designed (and ideal) for LED control, this board is NOT good for driving servos. Only three "SPI" pins are required to send data (our Arduino library shows how to to use any digital microcontroller pins). Best of all, the design is completely chainable. As long as there's enough power for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
  Lithium Ion Cylindrical Battery 3.7v 2200mAh: This lithium ion battery has a capacity of 2200mAh and a protection circuit that provides over-voltage, under-voltage and over-current protection. This cell can provide 2C of peak current (4400mA). Note that these batteries are not designed to sustain such high loads, we suggest keeping any constant current draw under about 0.5C (1 Amp).
  2.1mm DC Barrel Jack: 2.1mm DC Barrel Jack with Thru-Hole Connectors (breadboardable)
  RGB Strip LED: A tri-color Strip LED with red, green and blue. Based on LED SMD 5050 RGB Pin order: common cathode - green - red - blue
  Adafruit MAX9744 20W Amplifier: Pump up the volume with this 20W stereo amplifier! This slim little board has a class D amplifier onboard that can drive 2 channels of 4-8 ohm impedance speakers at 20W each. Power it with 5-12VDC using the onboard DC power jack and plug stereo line level into the 3.5mm stereo headphone jack and jam out with ease. Since it's class D, its completely cool-running, no heat sinks are required and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
