# Fritzing sketch Amiacs Light Controller (saved by Fritzing 0.9.3b)
breadboards: 2

parts:
  Ambient_RGB_LED_Strip = RGB Strip LED
  Part1 = Arduino Nano (Rev3.0)
  Trackball = RGB LED (com. cathode, rgb) [package="5 mm [THT]"]
  R1 = Resistor [tolerance=±5% resistance=220 package=THT]
  R2 = Resistor [tolerance=±5% resistance=220 package=THT]
  R3 = Resistor [tolerance=±5% resistance=220 package=THT]
  Q1 = Basic FET N-Channel [package="TO220 [THT]"]
  HLK-PM1 = HLK-PM12 [part_number=HLK-PM12]
  R4 = Resistor [tolerance=±5% resistance=220 package=THT]
  J2 = Camdenboss CTB0158-4 [part_number=CTB0158-4 package=THT]
  J3 = Camdenboss CTB0158-2 [part_number=CTB0158-2 package=THT]
  J5 = male pin header, 4 pins [form="♂ (male)"]
  J6 = male pin header, 4 pins [form="♂ (male)"]  # not connected
  Marquee_White_LED_Strip = LED - 5mm [color="White (6500K)" package="5 mm [THT]"]

nets:
  N1: Ambient_RGB_LED_Strip.Common_Connect, J2.terminal_4
  N2: Ambient_RGB_LED_Strip.Green_Connect, J2.terminal_3
  N3: Ambient_RGB_LED_Strip.Red_Connect, J2.terminal_2
  N4: Ambient_RGB_LED_Strip.Blue_Connect, J2.terminal_1
  N5: Part1.GND, Trackball.common_cathode, J5.pin1
  N6: Part1.D3, R1.Pin_1
  N7: Part1.D5, R2.Pin_1
  N8: Part1.D6, R3.Pin_1
  N9: Part1.D9, R4.Pin_1
  N10: Part1.D11/MOSI, J5.pin3
  N11: Part1.5V, J5.pin2
  N12: Part1.D13/SCK, J5.pin4
  N13: Trackball.red_anode, R1.Pin_0
  N14: Trackball.green_anode, R2.Pin_0
  N15: Trackball.blue_anode, R3.Pin_0
  N16: Q1.gate, R4.Pin_0
  N17: Q1.drain, Marquee_White_LED_Strip.cathode
  N18: Q1.source, HLK-PM1.-Vo, J3.terminal_2
  N19: HLK-PM1.+Vo, J3.terminal_1, Marquee_White_LED_Strip.anode

notes:
  The actual trackball LEDs do not require resistors.
  This group of parts represents an SPI based P9813 LED strip driver board.
  MOSI
  SCK
  CIN
  DIN
  VCC
  GND

custom parts:
  RGB Strip LED: A tri-color Strip LED with red, green and blue. Based on LED SMD 5050 RGB Pin order: common cathode - green - red - blue
