# Fritzing sketch Test Amiacs Light Controller (saved by Fritzing 0.9.3b)
breadboards: 4

parts:
  Ambient_RGB_LED_Strip = RGB Strip LED
  Part1 = Arduino Nano (Rev3.0)
  Trackball = RGB LED (com. cathode, rgb) [package="5 mm [THT]"]
  R1 = Resistor [tolerance=±5% resistance=220 package=THT]
  R2 = Resistor [tolerance=±5% resistance=220 package=THT]
  R3 = Resistor [tolerance=±5% resistance=220 package=THT]
  Q1 = Basic FET N-Channel [package="TO220 [THT]"]
  HLK-PM1 = HLK-PM12 [part_number=HLK-PM12]
  R4 = Resistor [tolerance=±5% resistance=220 package=THT]
  J2 = Camdenboss CTB0158-4 [part_number=CTB0158-4 package=THT]
  J3 = Camdenboss CTB0158-2 [part_number=CTB0158-2 package=THT]
  J5 = male pin header, 4 pins [form="♂ (male)"]
  J6 = male pin header, 4 pins [form="♂ (male)"]  # not connected
  Marquee_White_LED_Strip = LED - 5mm [color="White (6500K)" package="5 mm [THT]"]
  IC3 = MCP23017 I2C I/O Expander
  R21 = Resistor [tolerance=±5% resistance=220 package=THT]
  R22 = Resistor [tolerance=±5% resistance=220 package=THT]
  R23 = Resistor [tolerance=±5% resistance=220 package=THT]
  R24 = Resistor [tolerance=±5% resistance=220 package=THT]
  LED21 = LED - 3mm [color="Blue (525nm)" package="3 mm [THT]"]
  LED22 = LED - 3mm [color="Blue (525nm)" package="3 mm [THT]"]
  LED23 = LED - 3mm [color="Blue (525nm)" package="3 mm [THT]"]
  LED24 = LED - 3mm [color="Blue (525nm)" package="3 mm [THT]"]
  LED25 = LED - 3mm [color="Blue (525nm)" package="3 mm [THT]"]
  LED26 = LED - 3mm [color="Blue (525nm)" package="3 mm [THT]"]
  LED27 = LED - 3mm [color="Blue (525nm)" package="3 mm [THT]"]
  LED28 = LED - 3mm [color="Blue (525nm)" package="3 mm [THT]"]
  R25 = Resistor [tolerance=±5% resistance=220 package=THT]
  R26 = Resistor [tolerance=±5% resistance=220 package=THT]
  R27 = Resistor [tolerance=±5% resistance=220 package=THT]
  R28 = Resistor [tolerance=±5% resistance=220 package=THT]
  R29 = Resistor [tolerance=±5% resistance=220 package=THT]
  LED29 = LED - 3mm [color="Blue (525nm)" package="3 mm [THT]"]
  R30 = Resistor [tolerance=±5% resistance=220 package=THT]
  LED30 = LED - 3mm [color="Blue (525nm)" package="3 mm [THT]"]
  IC4 = MCP23017 I2C I/O Expander
  R31 = Resistor [tolerance=±5% resistance=220 package=THT]
  R32 = Resistor [tolerance=±5% resistance=220 package=THT]
  R33 = Resistor [tolerance=±5% resistance=220 package=THT]
  R34 = Resistor [tolerance=±5% resistance=220 package=THT]
  LED31 = LED - 3mm [color="Red (633nm)" package="3 mm [THT]"]
  LED32 = LED - 3mm [color="Red (633nm)" package="3 mm [THT]"]
  LED33 = LED - 3mm [color="Red (633nm)" package="3 mm [THT]"]
  LED34 = LED - 3mm [color="Red (633nm)" package="3 mm [THT]"]
  LED35 = LED - 3mm [color="Red (633nm)" package="3 mm [THT]"]
  LED36 = LED - 3mm [color="Red (633nm)" package="3 mm [THT]"]
  LED37 = LED - 3mm [color="Red (633nm)" package="3 mm [THT]"]
  LED38 = LED - 3mm [color="Red (633nm)" package="3 mm [THT]"]
  R35 = Resistor [tolerance=±5% resistance=220 package=THT]
  R36 = Resistor [tolerance=±5% resistance=220 package=THT]
  R37 = Resistor [tolerance=±5% resistance=220 package=THT]
  R38 = Resistor [tolerance=±5% resistance=220 package=THT]
  R39 = Resistor [tolerance=±5% resistance=220 package=THT]
  LED39 = LED - 3mm [color="Red (633nm)" package="3 mm [THT]"]
  R40 = Resistor [tolerance=±5% resistance=220 package=THT]
  LED40 = LED - 3mm [color="Red (633nm)" package="3 mm [THT]"]
  LED41 = LED - 3mm [color="Yellow (595nm)" package="3 mm [THT]"]
  LED42 = LED - 3mm [color="Yellow (595nm)" package="3 mm [THT]"]
  LED43 = LED - 3mm [color="Yellow (595nm)" package="3 mm [THT]"]
  LED44 = LED - 3mm [color="Yellow (595nm)" package="3 mm [THT]"]
  R41 = Resistor [tolerance=±5% resistance=220 package=THT]
  R42 = Resistor [tolerance=±5% resistance=220 package=THT]
  R43 = Resistor [tolerance=±5% resistance=220 package=THT]
  R44 = Resistor [tolerance=±5% resistance=220 package=THT]

nets:
  N1: Ambient_RGB_LED_Strip.Common_Connect, J2.terminal_4
  N2: Ambient_RGB_LED_Strip.Green_Connect, J2.terminal_3
  N3: Ambient_RGB_LED_Strip.Red_Connect, J2.terminal_2
  N4: Ambient_RGB_LED_Strip.Blue_Connect, J2.terminal_1
  GND: Part1.GND, Trackball.common_cathode, J5.pin1, IC3.A0, IC3.A1, IC3.A2, R25.Pin_1, R26.Pin_1, R27.Pin_1, R28.Pin_1, R29.Pin_1, R30.Pin_1, IC4.VSS, IC4.A1, IC4.A2, R31.Pin_1, R32.Pin_1, R33.Pin_1, R34.Pin_1, R35.Pin_1, R36.Pin_1, R37.Pin_1, R38.Pin_1, R39.Pin_1, R40.Pin_1, R43.Pin_0, R44.Pin_0
  N5: Part1.D3, R1.Pin_1
  N6: Part1.D5, R2.Pin_1
  N7: Part1.D6, R3.Pin_1
  N8: Part1.D9, R4.Pin_1
  N9: Part1.D11/MOSI, J5.pin3
  5V: Part1.5V, J5.pin2, IC3.RESET, IC4.VDD, IC4.A0, IC4.RESET
  N10: Part1.A5, IC3.SCL, IC4.SCL
  N11: Part1.A4, IC3.SDA, IC4.SDA
  N12: Part1.D13/SCK, J5.pin4
  N13: Trackball.red_anode, R1.Pin_0
  N14: Trackball.green_anode, R2.Pin_0
  N15: Trackball.blue_anode, R3.Pin_0
  N16: Q1.gate, R4.Pin_0
  N17: Q1.drain, Marquee_White_LED_Strip.cathode
  N18: Q1.source, HLK-PM1.-Vo, J3.terminal_2
  N19: HLK-PM1.+Vo, J3.terminal_1, Marquee_White_LED_Strip.anode
  N20: IC3.GPB0, LED30.anode
  N21: IC3.GPB1, LED29.anode
  N22: IC3.GPB2, LED42.anode
  N23: IC3.GPB3, LED41.anode
  N24: IC3.VSS, R21.Pin_1, R22.Pin_1, R23.Pin_1, R24.Pin_1, R41.Pin_0, R42.Pin_0
  N25: IC3.GPA0, LED25.anode
  N26: IC3.GPA1, LED27.anode
  N27: IC3.GPA2, LED26.anode
  N28: IC3.GPA3, LED24.anode
  N29: IC3.GPA4, LED21.anode
  N30: IC3.GPA5, LED22.anode
  N31: IC3.GPA6, LED23.anode
  N32: IC3.GPA7, LED28.anode
  N33: R21.Pin_0, LED23.cathode
  N34: R22.Pin_0, LED28.cathode
  N35: R23.Pin_0, LED22.cathode
  N36: R24.Pin_0, LED21.cathode
  N37: LED24.cathode, R27.Pin_0
  N38: LED25.cathode, R25.Pin_0
  N39: LED26.cathode, R28.Pin_0
  N40: LED27.cathode, R29.Pin_0
  N41: R26.Pin_0, LED29.cathode
  N42: R30.Pin_0, LED30.cathode
  N43: IC4.GPB0, LED40.anode
  N44: IC4.GPB1, LED39.anode
  N45: IC4.GPB2, LED43.anode
  N46: IC4.GPB3, LED44.anode
  N47: IC4.GPA0, LED35.anode
  N48: IC4.GPA1, LED37.anode
  N49: IC4.GPA2, LED36.anode
  N50: IC4.GPA3, LED34.anode
  N51: IC4.GPA4, LED31.anode
  N52: IC4.GPA5, LED32.anode
  N53: IC4.GPA6, LED33.anode
  N54: IC4.GPA7, LED38.anode
  N55: R31.Pin_0, LED33.cathode
  N56: R32.Pin_0, LED38.cathode
  N57: R33.Pin_0, LED32.cathode
  N58: R34.Pin_0, LED31.cathode
  N59: LED34.cathode, R39.Pin_0
  N60: LED35.cathode, R40.Pin_0
  N61: LED36.cathode, R35.Pin_0
  N62: LED37.cathode, R36.Pin_0
  N63: R37.Pin_0, LED39.cathode
  N64: R38.Pin_0, LED40.cathode
  N65: LED41.cathode, R42.Pin_1
  N66: LED42.cathode, R41.Pin_1
  N67: LED43.cathode, R43.Pin_1
  N68: LED44.cathode, R44.Pin_1

notes:
  The actual trackball LEDs do not require resistors.
  This group of parts represents an SPI based P9813 LED strip driver board.
  MOSI
  SCK
  CIN
  DIN
  VCC
  GND
  SDA
  SCL

custom parts:
  RGB Strip LED: A tri-color Strip LED with red, green and blue. Based on LED SMD 5050 RGB Pin order: common cathode - green - red - blue
  MCP23017 I2C I/O Expander: The MCP23017 uses two i2c pins (these can be shared with other i2c devices), and in exchange gives you 16 general purpose pins. You can set each of 16 pins to be input, output, input with a pullup or open drain. There's even the ability to get an interrupt via an external pin when any of the inputs change so you don't have to keep polling the chip.
