# Fritzing sketch Test MCP23017 Arcade Button LEDs (saved by Fritzing 0.9.3b)
breadboards: 2

parts:
  IC1 = MCP23017 I2C I/O Expander
  R1 = Resistor [tolerance=±5% resistance=220 package=THT]
  LED1 = LED - 3mm [color="Blue (525nm)" package="3 mm [THT]"]
  LED2 = LED - 3mm [color="Blue (525nm)" package="3 mm [THT]"]
  LED3 = LED - 3mm [color="Blue (525nm)" package="3 mm [THT]"]
  LED4 = LED - 3mm [color="Blue (525nm)" package="3 mm [THT]"]
  LED5 = LED - 3mm [color="Blue (525nm)" package="3 mm [THT]"]
  LED6 = LED - 3mm [color="Blue (525nm)" package="3 mm [THT]"]
  LED7 = LED - 3mm [color="Blue (525nm)" package="3 mm [THT]"]
  LED8 = LED - 3mm [color="Blue (525nm)" package="3 mm [THT]"]
  LED9 = LED - 3mm [color="Blue (525nm)" package="3 mm [THT]"]
  LED10 = LED - 3mm [color="Blue (525nm)" package="3 mm [THT]"]
  R2 = Resistor [tolerance=±5% resistance=220 package=THT]
  R3 = Resistor [tolerance=±5% resistance=220 package=THT]
  R4 = Resistor [tolerance=±5% resistance=220 package=THT]
  R5 = Resistor [tolerance=±5% resistance=220 package=THT]
  R6 = Resistor [tolerance=±5% resistance=220 package=THT]
  R7 = Resistor [tolerance=±5% resistance=220 package=THT]
  R8 = Resistor [tolerance=±5% resistance=220 package=THT]
  R9 = Resistor [tolerance=±5% resistance=220 package=THT]
  R10 = Resistor [tolerance=±5% resistance=220 package=THT]
  IC2 = MCP23017 I2C I/O Expander
  R11 = Resistor [tolerance=±5% resistance=220 package=THT]
  R12 = Resistor [tolerance=±5% resistance=220 package=THT]
  R13 = Resistor [tolerance=±5% resistance=220 package=THT]
  R14 = Resistor [tolerance=±5% resistance=220 package=THT]
  LED11 = LED - 3mm [color="Red (633nm)" package="3 mm [THT]"]
  LED12 = LED - 3mm [color="Red (633nm)" package="3 mm [THT]"]
  LED13 = LED - 3mm [color="Red (633nm)" package="3 mm [THT]"]
  LED14 = LED - 3mm [color="Red (633nm)" package="3 mm [THT]"]
  LED15 = LED - 3mm [color="Red (633nm)" package="3 mm [THT]"]
  LED16 = LED - 3mm [color="Red (633nm)" package="3 mm [THT]"]
  LED17 = LED - 3mm [color="Red (633nm)" package="3 mm [THT]"]
  LED18 = LED - 3mm [color="Red (633nm)" package="3 mm [THT]"]
  R15 = Resistor [tolerance=±5% resistance=220 package=THT]
  R16 = Resistor [tolerance=±5% resistance=220 package=THT]
  R17 = Resistor [tolerance=±5% resistance=220 package=THT]
  R18 = Resistor [tolerance=±5% resistance=220 package=THT]
  R19 = Resistor [tolerance=±5% resistance=220 package=THT]
  LED19 = LED - 3mm [color="Red (633nm)" package="3 mm [THT]"]
  R20 = Resistor [tolerance=±5% resistance=220 package=THT]
  LED20 = LED - 3mm [color="Red (633nm)" package="3 mm [THT]"]
  Part1 = Arduino Nano (Rev3.0)

nets:
  N1: IC1.GPB0, LED1.anode
  N2: IC1.GPB1, LED2.anode
  N3: IC1.VSS, R1.Pin_1, R2.Pin_1, R3.Pin_1, R4.Pin_1
  N4: IC1.SCL, IC2.SCL, Part1.A6, Part1.A5
  N5: IC1.SDA, IC2.SDA, Part1.A4
  VSS: IC1.A0, IC1.A1, IC1.A2, R5.Pin_1, R6.Pin_1, R7.Pin_1, R8.Pin_1, R9.Pin_1, R10.Pin_1, IC2.VSS, IC2.A1, IC2.A2, R11.Pin_1, R12.Pin_1, R13.Pin_1, R14.Pin_1, R15.Pin_1, R16.Pin_1, R17.Pin_1, R18.Pin_1, R19.Pin_1, R20.Pin_1, Part1.VIN, Part1.GND
  VDD: IC1.RESET, IC2.VDD, IC2.A0, IC2.RESET, Part1.RESET, Part1.5V
  N6: IC1.GPA0, LED3.anode
  N7: IC1.GPA1, LED4.anode
  N8: IC1.GPA2, LED5.anode
  N9: IC1.GPA3, LED6.anode
  N10: IC1.GPA4, LED7.anode
  N11: IC1.GPA5, LED8.anode
  N12: IC1.GPA6, LED9.anode
  N13: IC1.GPA7, LED10.anode
  N14: R1.Pin_0, LED7.cathode
  N15: LED1.cathode, R10.Pin_0
  N16: LED2.cathode, R9.Pin_0
  N17: LED3.cathode, R5.Pin_0
  N18: LED4.cathode, R6.Pin_0
  N19: LED5.cathode, R7.Pin_0
  N20: LED6.cathode, R8.Pin_0
  N21: LED8.cathode, R2.Pin_0
  N22: LED9.cathode, R3.Pin_0
  N23: LED10.cathode, R4.Pin_0
  N24: IC2.GPB0, LED20.anode
  N25: IC2.GPB1, LED19.anode
  N26: IC2.GPA0, LED15.anode
  N27: IC2.GPA1, LED17.anode
  N28: IC2.GPA2, LED16.anode
  N29: IC2.GPA3, LED14.anode
  N30: IC2.GPA4, LED11.anode
  N31: IC2.GPA5, LED12.anode
  N32: IC2.GPA6, LED13.anode
  N33: IC2.GPA7, LED18.anode
  N34: R11.Pin_0, LED13.cathode
  N35: R12.Pin_0, LED18.cathode
  N36: R13.Pin_0, LED12.cathode
  N37: R14.Pin_0, LED11.cathode
  N38: LED14.cathode, R19.Pin_0
  N39: LED15.cathode, R20.Pin_0
  N40: LED16.cathode, R15.Pin_0
  N41: LED17.cathode, R16.Pin_0
  N42: R17.Pin_0, LED19.cathode
  N43: R18.Pin_0, LED20.cathode

custom parts:
  MCP23017 I2C I/O Expander: The MCP23017 uses two i2c pins (these can be shared with other i2c devices), and in exchange gives you 16 general purpose pins. You can set each of 16 pins to be input, output, input with a pullup or open drain. There's even the ability to get an interrupt via an external pin when any of the inputs change so you don't have to keep polling the chip.

// code stored in the sketch: Test_MCP23017_Arcade_Button_LEDs.ino
// Based on Blink-a-tron from http://www.retrobuiltgames.com/porta-pi-arcade-help/blinky-led-buttons/
// Schematic drawn in Tinkercad Circuits as "Test Arcade Button LEDs".
// https://www.tinkercad.com/things/3QHra1MhREQ-test-arcade-button-leds

#include <Wire.h>
#include <Adafruit_MCP23017.h>

#define playerColumns 5
#define playerRows 3
#define playerMaximumPins 16

Adafruit_MCP23017 player1;
Adafruit_MCP23017 player2;

int player1LedArray[playerRows][playerColumns] =
{
  {8, 9, -1, -1, -1},
  {-1, 0, 1, 2, 3},
  {-1, 4, 5, 6, 7}
};

int player2LedArray[playerRows][playerColumns] =
{
  {-1, -1, -1, 8, 9},
  {0, 1, 2, 3, -1},
  {4, 5, 6, 7, -1}
};

void setup() {
  player1.begin(0);
  player1.writeGPIOAB(0);
  for (int pin = 0; pin < playerMaximumPins; pin++)
  {
    player1.pinMode(pin, OUTPUT);
  }

  player2.begin(1);
  player2.writeGPIOAB(0);
  for (int pin = 0; pin < playerMaximumPins; pin++)
  {
    player2.pinMode(pin, OUTPUT);
  }

//  player2.pinMode(0, OUTPUT);
//  player2.pullUp(0, HIGH);
//  player2.digitalWrite(0, HIGH);

//  pinMode(3, OUTPUT);
//  digitalWrite(3, HIGH);
//  analogWrite(3, 8);

//  initializeUsingWire();
}

void loop() {
  unsigned long startTime = millis();

  while(millis() - startTime < 10000)
  {
    randomTogglePin(10);
  }

  delay(100);

  allPlayerDigitalWrite(HIGH);

  for(int delayTime = 250; delayTime > 0; delayTime -= 25)
  {
    allFlash(delayTime);
  }

  delay(100);

  for(int delayTime = 150; delayTime > 0; delayTime -= 25)
  {
    useArray(delayTime);
  }

  delay(100);

  for(int delayTime = 250; delayTime > 0; delayTime -= 25)
  {
    entireRow(delayTime);
  }

  delay(100);

  inOrder(500);

//  testUsingWire();
}

int getPlayerPin(int row, int column)
{
  int playerPin = -1;

  if (row >= 0 && row < playerRows)
  {
    if (column >= 0 && column < playerColumns)
    {
      playerPin = player1LedArray[row][column];
    }
    else if (column >= playerColumns && column < 2 * playerColumns)
    {
      playerPin = player2LedArray[row][column - playerColumns];
    }
  }

  return playerPin;
}

void playerPinDigitalWrite(int row, int column, int mode)
{
  int playerPin = getPlayerPin(row, column);

  if (playerPin >= 0 && playerPin < playerMaximumPins)
  {
    if (column < playerColumns)
    {
      player1.digitalWrite(playerPin, mode);
    }
    else
    {
      player2.digitalWrite(playerPin, mode);
    }
  }
}

int playerPinDigitalRead(int row, int column)
{
  int mode = LOW;
  int playerPin = getPlayerPin(row, column);

  if (playerPin >= 0 && playerPin < playerMaximumPins)
  {
    if (column < playerColumns)
    {
      mode = player1.digitalRead(playerPin);
    }
    else
    {
      mode = player2.digitalRead(playerPin);
    }
  }

  return mode;
}

void allPlayerDigitalWrite(int mode)
{
  for (int row = 0; row < playerRows; row++)
  {
    for (int column = 0; column < 2 * playerColumns; column++)
    {
      playerPinDigitalWrite(row, column, mode);
    }
  }
}

void randomTogglePin(int delayTime)
{
  int row = random(playerRows);
  int column = random(2 * playerColumns);

  if (getPlayerPin(row, column) != -1)
  {
    if (playerPinDigitalRead(row, column) == LOW)
    {
      playerPinDigitalWrite(row, column, HIGH);
    }
    else if (playerPinDigitalRead(row, column) == HIGH)
    {
      playerPinDigitalWrite(row, column, LOW);
    }

    delay(delayTime);
  }
}

void allFlash(int delayTime)
{
  allPlayerDigitalWrite(HIGH);

  delay(delayTime);

  allPlayerDigitalWrite(LOW);

  delay(delayTime);
}

void entireRow(int delayTime)
{
  for (int row = 0; row < playerRows; row++)
  {
    for (int column = 0; column < 2 * playerColumns; column++)
    {
      playerPinDigitalWrite(row, column, HIGH);
    }

    delay(delayTime);

    for (int column = 0; column < 2 * playerColumns; column++)
    {
      playerPinDigitalWrite(row, column, LOW);
    }
  }
}

void useArray(int delayTime)
{
  for (int row = 0; row < playerRows; row++)
  {
    for (int column = 0; column < 2 * playerColumns; column++)
    {
      playerPinDigitalWrite(row, column, HIGH);

      if (getPlayerPin(row, column) != -1)
      {
        delay(delayTime);
      }

      playerPinDigitalWrite(row, column, LOW);
    }
  }
}

void inOrder(int delayTime)
{
  for (int pin = 0; pin < playerMaximumPins; pin++)
  {
    player1.digitalWrite(pin, HIGH);
    player2.digitalWrite(pin, HIGH);
    delay(delayTime);
    player1.digitalWrite(pin, LOW);
    player2.digitalWrite(pin, LOW);
  }
}


void initializeUsingWire()
{
  Wire.begin();
  Wire.beginTransmission(0x20);
  Wire.write(0x00);
  Wire.write(0x00);
  Wire.endTransmission();
  Wire.beginTransmission(0x20);
  Wire.write(0x01);
  Wire.write(0x00);
  Wire.endTransmission();
}

void testUsingWire()
{
  Wire.beginTransmission(0x20);
  Wire.write(0x12);
  Wire.write(0);
  Wire.endTransmission();

  Wire.beginTransmission(0x20);
  Wire.write(0x13);
  Wire.write(0);
  Wire.endTransmission();

  for (int i = 0; i <= 7; i++)
  {
    Wire.beginTransmission(0x20);
    Wire.write(0x12);
    Wire.write(bit(i));
    Wire.endTransmission();
    delay(500);
  }

  Wire.beginTransmission(0x20);
  Wire.write(0x12);
  Wire.write(0);
  Wire.endTransmission();

  for (int i = 0; i <= 7; i++)
  {
    Wire.beginTransmission(0x20);
    Wire.write(0x13);
    Wire.write(bit(i));
    Wire.endTransmission();
    delay(500);
  }
}

// code stored in the sketch: test_mcp23017_arcadebuttons.ino
// Based on Blink-a-tron from http://www.retrobuiltgames.com/porta-pi-arcade-help/blinky-led-buttons/
// Schematic drawn in Tinkercad Circuits as "Test Arcade Button LEDs".
// https://www.tinkercad.com/things/3QHra1MhREQ-test-arcade-button-leds

#include <Wire.h>
#include <Adafruit_MCP23017.h>

#define playerColumns 5
#define playerRows 3
#define playerMaximumPins 16

Adafruit_MCP23017 player1;
Adafruit_MCP23017 player2;

int player1LedArray[playerRows][playerColumns] =
{
  {8, 9, -1, -1, -1},
  {-1, 0, 1, 2, 3},
  {-1, 4, 5, 6, 7}
};

int player2LedArray[playerRows][playerColumns] =
{
  {-1, -1, -1, 8, 9},
  {0, 1, 2, 3, -1},
  {4, 5, 6, 7, -1}
};

void setup() {
  player1.begin(0);
  player1.writeGPIOAB(0);
  for (int pin = 0; pin < playerMaximumPins; pin++)
  {
    player1.pinMode(pin, OUTPUT);
  }

  player2.begin(1);
  player2.writeGPIOAB(0);
  for (int pin = 0; pin < playerMaximumPins; pin++)
  {
    player2.pinMode(pin, OUTPUT);
  }

//  player2.pinMode(0, OUTPUT);
//  player2.pullUp(0, HIGH);
//  player2.digitalWrite(0, HIGH);

//  pinMode(3, OUTPUT);
//  digitalWrite(3, HIGH);
//  analogWrite(3, 8);

//  initializeUsingWire();
}

void loop() {
  unsigned long startTime = millis();

  while(millis() - startTime < 10000)
  {
    randomTogglePin(10);
  }

  delay(100);

  allPlayerDigitalWrite(HIGH);

  for(int delayTime = 250; delayTime > 0; delayTime -= 25)
  {
    allFlash(delayTime);
  }

  delay(100);

  for(int delayTime = 150; delayTime > 0; delayTime -= 25)
  {
    useArray(delayTime);
  }

  delay(100);

  for(int delayTime = 250; delayTime > 0; delayTime -= 25)
  {
    entireRow(delayTime);
  }

  delay(100);

  inOrder(500);

//  testUsingWire();
}

int getPlayerPin(int row, int column)
{
  int playerPin = -1;

  if (row >= 0 && row < playerRows)
  {
    if (column >= 0 && column < playerColumns)
    {
      playerPin = player1LedArray[row][column];
    }
    else if (column >= playerColumns && column < 2 * playerColumns)
    {
      playerPin = player2LedArray[row][column - playerColumns];
    }
  }

  return playerPin;
}

void playerPinDigitalWrite(int row, int column, int mode)
{
  int playerPin = getPlayerPin(row, column);

  if (playerPin >= 0 && playerPin < playerMaximumPins)
  {
    if (column < playerColumns)
    {
      player1.digitalWrite(playerPin, mode);
    }
    else
    {
      player2.digitalWrite(playerPin, mode);
    }
  }
}

int playerPinDigitalRead(int row, int column)
{
  int mode = LOW;
  int playerPin = getPlayerPin(row, column);

  if (playerPin >= 0 && playerPin < playerMaximumPins)
  {
    if (column < playerColumns)
    {
      mode = player1.digitalRead(playerPin);
    }
    else
    {
      mode = player2.digitalRead(playerPin);
    }
  }

  return mode;
}

void allPlayerDigitalWrite(int mode)
{
  for (int row = 0; row < playerRows; row++)
  {
    for (int column = 0; column < 2 * playerColumns; column++)
    {
      playerPinDigitalWrite(row, column, mode);
    }
  }
}

void randomTogglePin(int delayTime)
{
  int row = random(playerRows);
  int column = random(2 * playerColumns);

  if (getPlayerPin(row, column) != -1)
  {
    if (playerPinDigitalRead(row, column) == LOW)
    {
      playerPinDigitalWrite(row, column, HIGH);
    }
    else if (playerPinDigitalRead(row, column) == HIGH)
    {
      playerPinDigitalWrite(row, column, LOW);
    }

    delay(delayTime);
  }
}

void allFlash(int delayTime)
{
  allPlayerDigitalWrite(HIGH);

  delay(delayTime);

  allPlayerDigitalWrite(LOW);

  delay(delayTime);
}

void entireRow(int delayTime)
{
  for (int row = 0; row < playerRows; row++)
  {
    for (int column = 0; column < 2 * playerColumns; column++)
    {
      playerPinDigitalWrite(row, column, HIGH);
    }

    delay(delayTime);

    for (int column = 0; column < 2 * playerColumns; column++)
    {
      playerPinDigitalWrite(row, column, LOW);
    }
  }
}

void useArray(int delayTime)
{
  for (int row = 0; row < playerRows; row++)
  {
    for (int column = 0; column < 2 * playerColumns; column++)
    {
      playerPinDigitalWrite(row, column, HIGH);

      if (getPlayerPin(row, column) != -1)
      {
        delay(delayTime);
      }

      playerPinDigitalWrite(row, column, LOW);
    }
  }
}

void inOrder(int delayTime)
{
  for (int pin = 0; pin < playerMaximumPins; pin++)
  {
    player1.digitalWrite(pin, HIGH);
    player2.digitalWrite(pin, HIGH);
    delay(delayTime);
    player1.digitalWrite(pin, LOW);
    player2.digitalWrite(pin, LOW);
  }
}


void initializeUsingWire()
{
  Wire.begin();
  Wire.beginTransmission(0x20);
  Wire.write(0x00);
  Wire.write(0x00);
  Wire.endTransmission();
  Wire.beginTransmission(0x20);
  Wire.write(0x01);
  Wire.write(0x00);
  Wire.endTransmission();
}

void testUsingWire()
{
  Wire.beginTransmission(0x20);
  Wire.write(0x12);
  Wire.write(0);
  Wire.endTransmission();

  Wire.beginTransmission(0x20);
  Wire.write(0x13);
  Wire.write(0);
  Wire.endTransmission();

  for (int i = 0; i <= 7; i++)
  {
    Wire.beginTransmission(0x20);
    Wire.write(0x12);
    Wire.write(bit(i));
    Wire.endTransmission();
    delay(500);
  }

  Wire.beginTransmission(0x20);
  Wire.write(0x12);
  Wire.write(0);
  Wire.endTransmission();

  for (int i = 0; i <= 7; i++)
  {
    Wire.beginTransmission(0x20);
    Wire.write(0x13);
    Wire.write(bit(i));
    Wire.endTransmission();
    delay(500);
  }
}
